# Fritzing sketch schematic (saved by Fritzing 1.0.7)

parts:
  A1 = Raspberry Pi 5
  J1 = Basic Servo
  Power_plug1 = Power plug
  DRV_1 = DRV 8825 Stepper Motor Carrier, High Current [part_number="DRV 8825"]
  M1 = Stepper Motor - Bipolar

nets (from the breadboard view):
  N1: A1.3V3, DRV_1.VOLTAGE_DD
  5V: A1.5V, A1.Fan-5V, J1.vcc
  GND: A1.GND, J1.gnd, DRV_1.GROUND_LOG
  N2: A1.GPIO25, J1.pulse
  N3: A1.GPIO20, DRV_1.STEP
  N4: A1.GPIO21, DRV_1.DIRECTION
  N5: Power_plug1.VCC, DRV_1.VOLTAGE_ST/_MT
  N6: Power_plug1.GND, DRV_1.GROUND_ST/_MT
  N7: DRV_1.RESET, DRV_1.SLEEP
  N8: DRV_1.OUT_2B, M1.A
  N9: DRV_1.OUT_2A, M1.C
  N10: DRV_1.OUT_1A, M1.B
  N11: DRV_1.OUT_1B, M1.D

notes:
  USB connection to camera module
  USB 5V-5A Power

custom parts:
  Raspberry Pi 5: The RPi5, a faster version of the awesome Raspberry Pi4B ARM Board with 40 pin gpio.
